// Logisim project cpu.circ as structural Verilog: 2 circuits, main circuit main
module main (
  input  [31:0] INSTRUCTION,
  input  CLOCK,
  output [31:0] PROGRAM_COUNTER,
  output [31:0] ra,
  output [31:0] sp,
  output [31:0] t0,
  output [31:0] t1,
  output [31:0] t2,
  output [31:0] s0,
  output [31:0] s1,
  output [31:0] a0
);

  wire comparator_1_eq, DMEM_p4, undriven, undriven_2;
  wire [3:0] undriven_3;
  wire [4:0] rd_IF;
  wire [31:0] adder_1_out, alu_result, immi, multiplexer_1_out, multiplexer_2_out, multiplexer_3_out,
       Read_data, rs1_output, rs2_output, write_reg;

  imme imme_1 (.out_2(immi), .in_1(INSTRUCTION));
  Multiplexer #(.width(32), .enable("false")) multiplexer_1 (
    .in0(Read_data), .in1(alu_result), .out(multiplexer_1_out), .sel(1'b1));
  Register #(.width(5)) register_1 (.D(INSTRUCTION[11:7]), .en(1'b1), .clk(CLOCK), .Q(rd_IF));  // open: clr
  Adder #(.width(32)) adder_1 (.a(PROGRAM_COUNTER), .b(32'h4), .out(adder_1_out));  // open: cin, cout
  Register #(.width(32)) PC (.D(adder_1_out), .en(1'b1), .clk(CLOCK), .Q(PROGRAM_COUNTER));  // open: clr
  Register #(.width(32)) register_2 (.D(multiplexer_1_out), .en(1'b1), .clk(CLOCK), .Q(write_reg));  // open: clr
  regfile_main RegFile (
    .rs2(INSTRUCTION[24:20]), .rd(rd_IF), .Read_Data_1(rs1_output), .Read_Data_2(rs2_output), .ra(ra),
    .sp(sp), .t0(t0), .t1(t1), .t2(t2), .s0(s0), .s1(s1), .a0(a0), .rs1(INSTRUCTION[19:15]),
    .Write_Data(write_reg), .RegWEn(undriven), .clk(CLOCK));
  Comparator #(.width(5)) comparator_1 (.a(INSTRUCTION[19:15]), .b(rd_IF), .eq(comparator_1_eq));  // open: gt, lt
  Multiplexer #(.width(32), .enable("false")) multiplexer_2 (
    .in0(immi), .in1(rs2_output), .out(multiplexer_2_out), .sel(undriven_2));
  Multiplexer #(.width(32), .enable("false")) multiplexer_3 (
    .in0(rs1_output), .in1(write_reg), .out(multiplexer_3_out), .sel(comparator_1_eq));
  alu Arithmetic_Logic_Unit (.ALUSel(undriven_3), .B(multiplexer_2_out), .A(multiplexer_3_out), .Result(alu_result));
  // mem_main DMEM: pin names not known; wires that end beside it: alu_result, rs2_output, CLOCK, DMEM_p4, DMEM_p4, Read_data

  // Other names for the same wires on the sheet: clk = CLOCK; opcode[6:0] = INSTRUCTION[6:0];
  //   rd[4:0] = INSTRUCTION[11:7]; funct3[2:0] = INSTRUCTION[14:12]; rs1[4:0] = INSTRUCTION[19:15];
  //   rs2[4:0] = INSTRUCTION[24:20]; funct7[6:0] = INSTRUCTION[31:25]

  // Notes on the sheet:
  //   Output
  //   IMEM (do **NOT** move this)
  //   Inputs
  //   It is OK to move the PC, RegFile, ALU, and MEM to wherever is most convenient for you when constructing your CPU, and to delete this text
  //   Inputs/Outputs for testing. Do **NOT** move these.
endmodule

module imme (
  input  [31:0] in_1,
  output [31:0] out_2
);

  wire [31:11] I, S;
  wire [31:12] SB;
  wire [31:20] UJ;

  Multiplexer #(.width(21), .enable("false")) multiplexer_1 (
    .in0({21{1'b0}}), .in1({21{1'b1}}), .out(I), .sel(in_1[31]));
  Multiplexer #(.width(21), .enable("false")) multiplexer_2 (
    .in0({21{1'b0}}), .in1({21{1'b1}}), .out(S), .sel(in_1[31]));
  Multiplexer #(.width(20), .enable("false")) multiplexer_3 (
    .in0({20{1'b0}}), .in1({20{1'b1}}), .out(SB), .sel(in_1[31]));
  Multiplexer #(.width(12), .enable("false")) multiplexer_4 (
    .in0({12{1'b0}}), .in1({12{1'b1}}), .out(UJ), .sel(in_1[31]));
  Multiplexer #(.select(3), .width(32), .enable("false")) multiplexer_5 (
    .in0({I, in_1[30:20]}), .in1({S, in_1[30:25], in_1[11:7]}),
    .in3({SB, in_1[7], in_1[30:25], in_1[11:8], 1'b0}), .in5({in_1[31:12], {12{1'b0}}}),
    .in7({UJ, in_1[19:12], in_1[20], in_1[30:21], 1'b0}), .out(out_2), .sel({in_1[2], in_1[6:5]}));  // open: in2, in4, in6

  // Other names for the same wires on the sheet: INSTRUCTION[31:0] = in_1; immi[31:0] = out_2;
  //   S[10:0] = {in_1[30:25], in_1[11:7]}; SB[11:1] = {in_1[7], in_1[30:25], in_1[11:8]}; U[31:12] = in_1[31:12];
  //   I[10:0] = in_1[30:20]; UJ[19:1] = {in_1[19:12], in_1[20], in_1[30:21]}

  // Notes on the sheet:
  //   Output
  //   Inputs
endmodule
